// Logisim project Somadores.circ as structural Verilog: 9 circuits, main circuit main
module main (
  input  [1:0] XY,
  input  [3:0] A,
  input  [3:0] B,
  input  [2:0] in_4,
  output OverFlow,
  output OverFlow_2,
  output [3:0] out_7
);

  wire decodificador_3x8_1_s0, decodificador_3x8_1_s1, decodificador_3x8_1_s2, decodificador_3x8_1_s3;
  wire [3:0] \rotação_dir_1_abcd_2 , \rotação_esq_1_abcd_2 , somador_4bits_1_saida, subtrator_4bit_1_saida;

  Decodificador_3x8 decodificador_3x8_1 (
    .S0(decodificador_3x8_1_s0), .S1(decodificador_3x8_1_s1), .S2(decodificador_3x8_1_s2),
    .S3(decodificador_3x8_1_s3), .in_1(in_4));  // open: S4, S5, S6, S7
  Somador_4Bits somador_4bits_1 (.Overflow(OverFlow), .B(B), .A(A), .Saida(somador_4bits_1_saida));
  Buff buff_1 (.E(somador_4bits_1_saida), .in_2(decodificador_3x8_1_s0), .S(out_7));
  Subtrator_4Bit subtrator_4bit_1 (.B(B), .Overflow(OverFlow_2), .A(A), .Saida(subtrator_4bit_1_saida));
  Buff buff_2 (.E(subtrator_4bit_1_saida), .in_2(decodificador_3x8_1_s1), .S(out_7));
  \Rotação_Esq  \rotação_esq_1  (.ABCD(A), .XY(XY), .ABCD_2(\rotação_esq_1_abcd_2 ));
  \Rotação_Dir  \rotação_dir_1  (.ABCD(A), .XY(XY), .ABCD_2(\rotação_dir_1_abcd_2 ));
  Buff buff_3 (.E(\rotação_dir_1_abcd_2 ), .in_2(decodificador_3x8_1_s2), .S(out_7));
  // Probe on out_7
  Buff buff_4 (.E(\rotação_esq_1_abcd_2 ), .in_2(decodificador_3x8_1_s3), .S(out_7));
endmodule

module Somador_1Bit (
  input  A,
  input  B,
  input  C,
  output S,
  output Vai_1
);

  wire and_1_out, and_2_out, or_1_out, xor_1_out;

  xor xor_1 (xor_1_out, C, B);
  and and_1 (and_1_out, C, B);
  or or_1 (or_1_out, C, B);
  and and_2 (and_2_out, or_1_out, A);
  xor xor_2 (S, xor_1_out, A);
  or or_2 (Vai_1, and_1_out, and_2_out);
endmodule

module Somador_4Bits (
  input  [3:0] A,
  input  [3:0] B,
  output Overflow,
  output [3:0] Saida
);

  wire somador_1bit_2_vai_1, somador_1bit_3_vai_1, somador_1bit_4_vai_1;

  // Probe on B
  Somador_1Bit somador_1bit_1 (.S(Saida[3]), .Vai_1(Overflow), .A(A[3]), .B(B[3]), .C(somador_1bit_2_vai_1));
  Somador_1Bit somador_1bit_2 (
    .S(Saida[2]), .Vai_1(somador_1bit_2_vai_1), .A(A[2]), .B(B[2]), .C(somador_1bit_3_vai_1));
  // Probe on Saida
  Somador_1Bit somador_1bit_3 (
    .S(Saida[1]), .Vai_1(somador_1bit_3_vai_1), .A(A[1]), .B(B[1]), .C(somador_1bit_4_vai_1));
  Somador_1Bit somador_1bit_4 (.S(Saida[0]), .Vai_1(somador_1bit_4_vai_1), .A(A[0]), .B(B[0]), .C(1'b0));
  // Probe on A
endmodule

module Subtrator_1Bit (
  input  A,
  input  B,
  input  C,
  output S,
  output Vai_1
);

  wire and_1_out, and_2_out, or_1_out, xor_1_out;

  xor xor_1 (xor_1_out, C, B);
  and and_1 (and_1_out, C, B);
  or or_1 (or_1_out, C, B);
  and and_2 (and_2_out, or_1_out, ~A);  // AND_Gate
  xor xor_2 (S, xor_1_out, A);
  or or_2 (Vai_1, and_1_out, and_2_out);
endmodule

module Subtrator_4Bit (
  input  [3:0] A,
  input  [3:0] B,
  output Overflow,
  output [3:0] Saida
);

  wire subtrator_1bit_2_vai_1, subtrator_1bit_3_vai_1, subtrator_1bit_4_vai_1;

  // Probe on B
  Subtrator_1Bit subtrator_1bit_1 (.S(Saida[3]), .Vai_1(Overflow), .A(A[3]), .B(B[3]), .C(subtrator_1bit_2_vai_1));
  Subtrator_1Bit subtrator_1bit_2 (
    .S(Saida[2]), .Vai_1(subtrator_1bit_2_vai_1), .A(A[2]), .B(B[2]), .C(subtrator_1bit_3_vai_1));
  // Probe on Saida
  Subtrator_1Bit subtrator_1bit_3 (
    .S(Saida[1]), .Vai_1(subtrator_1bit_3_vai_1), .A(A[1]), .B(B[1]), .C(subtrator_1bit_4_vai_1));
  Subtrator_1Bit subtrator_1bit_4 (.S(Saida[0]), .Vai_1(subtrator_1bit_4_vai_1), .A(A[0]), .B(B[0]), .C(1'b0));
  // Probe on A
endmodule

module \Rotação_Esq  (
  input  [3:0] ABCD,
  input  [1:0] XY,
  output [3:0] ABCD_2
);

  wire and_1_out, and_2_out, and_3_out, and_4_out, and_5_out, and_6_out, and_7_out, and_8_out, and_9_out;

  and and_1 (and_1_out, ~XY[1], ~XY[0], ABCD[3]);  // AND_Gate
  and and_2 (and_2_out, ~XY[1], XY[0], ABCD[2]);  // AND_Gate
  and and_3 (and_3_out, XY[1], ~XY[0], ABCD[1]);  // AND_Gate
  and and_4 (and_4_out, XY[1], XY[0], ABCD[0]);
  and and_5 (and_5_out, ~XY[1], ~XY[0], ABCD[2]);  // AND_Gate
  and and_6 (and_6_out, ~XY[1], XY[0], ABCD[1]);  // AND_Gate
  and and_7 (and_7_out, XY[1], ~XY[0], ABCD[0]);  // AND_Gate
  and and_8 (and_8_out, ~XY[1], ~XY[0], ABCD[1]);  // AND_Gate
  and and_9 (and_9_out, ~XY[1], XY[0], ABCD[0]);  // AND_Gate
  and and_10 (ABCD_2[0], ~XY[1], ~XY[0], ABCD[0]);  // AND_Gate
  or or_1 (ABCD_2[3], and_1_out, and_2_out, and_3_out, and_4_out);
  or or_2 (ABCD_2[2], and_5_out, and_6_out, and_7_out);
  or or_3 (ABCD_2[1], and_8_out, and_9_out);
endmodule

module \Rotação_Dir  (
  input  [3:0] ABCD,
  input  [1:0] XY,
  output [3:0] ABCD_2
);

  wire and_1_out, and_2_out, and_3_out, and_4_out, and_5_out, and_6_out, and_7_out, and_8_out, and_9_out;

  and and_1 (and_1_out, ~XY[1], ~XY[0], ABCD[0]);  // AND_Gate
  and and_2 (and_2_out, ~XY[1], XY[0], ABCD[1]);  // AND_Gate
  and and_3 (and_3_out, XY[1], ~XY[0], ABCD[2]);  // AND_Gate
  and and_4 (and_4_out, XY[1], XY[0], ABCD[3]);
  and and_5 (and_5_out, ~XY[1], ~XY[0], ABCD[1]);  // AND_Gate
  and and_6 (and_6_out, ~XY[1], XY[0], ABCD[2]);  // AND_Gate
  and and_7 (and_7_out, XY[1], ~XY[0], ABCD[3]);  // AND_Gate
  and and_8 (and_8_out, ~XY[1], ~XY[0], ABCD[2]);  // AND_Gate
  and and_9 (and_9_out, ~XY[1], XY[0], ABCD[3]);  // AND_Gate
  and and_10 (ABCD_2[3], ~XY[1], ~XY[0], ABCD[3]);  // AND_Gate
  or or_1 (ABCD_2[0], and_1_out, and_2_out, and_3_out, and_4_out);
  or or_2 (ABCD_2[1], and_5_out, and_6_out, and_7_out);
  or or_3 (ABCD_2[2], and_8_out, and_9_out);
endmodule

module Buff (
  input  [3:0] E,
  input  in_2,
  output [3:0] S
);

  assign S[3] = in_2 ? E[3] : 1'bz;  // Controlled_Buffer controlled_buffer_1
  assign S[2] = in_2 ? E[2] : 1'bz;  // Controlled_Buffer controlled_buffer_2
  assign S[0] = in_2 ? E[0] : 1'bz;  // Controlled_Buffer controlled_buffer_3
  assign S[1] = in_2 ? E[1] : 1'bz;  // Controlled_Buffer controlled_buffer_4
endmodule

module Decodificador_3x8 (
  input  [2:0] in_1,
  output S0,
  output S1,
  output S2,
  output S3,
  output S4,
  output S5,
  output S6,
  output S7
);

  wire not_1_out, not_2_out, not_3_out, not_4_out, not_5_out, not_6_out, not_7_out, not_8_out, not_9_out,
       not_10_out, not_11_out, not_12_out;

  not not_1 (not_1_out, in_1[2]);
  not not_2 (not_2_out, in_1[1]);
  not not_3 (not_3_out, in_1[0]);
  not not_4 (not_4_out, in_1[2]);
  not not_5 (not_5_out, in_1[1]);
  not not_6 (not_6_out, in_1[2]);
  not not_7 (not_7_out, in_1[0]);
  not not_8 (not_8_out, in_1[2]);
  not not_9 (not_9_out, in_1[1]);
  not not_10 (not_10_out, in_1[0]);
  not not_11 (not_11_out, in_1[1]);
  not not_12 (not_12_out, in_1[0]);
  and and_1 (S7, in_1[2], in_1[1], in_1[0]);
  and and_2 (S0, not_1_out, not_2_out, not_3_out);
  and and_3 (S1, not_4_out, not_5_out, in_1[0]);
  and and_4 (S2, not_6_out, in_1[1], not_7_out);
  and and_5 (S3, not_8_out, in_1[1], in_1[0]);
  and and_6 (S4, in_1[2], not_9_out, not_10_out);
  and and_7 (S5, in_1[2], not_11_out, in_1[0]);
  and and_8 (S6, in_1[2], in_1[1], not_12_out);
endmodule
